// Logisim project 4Bit_Counter.circ as structural Verilog: 1 circuit, main circuit Bit4_Counter
module Bit4_Counter (
  input  INR,
  input  CP,
  input  CLR,
  output A0,
  output A1,
  output A2,
  output A3
);

  // Master_Slave_Flip_Flop master_slave_flip_flop_1: pin names not known; wires that end beside it: INR, INR, CP, CLR, A0
  // Master_Slave_Flip_Flop master_slave_flip_flop_2: pin names not known; wires that end beside it: INR, INR, A0, CLR, A1
  // Master_Slave_Flip_Flop master_slave_flip_flop_3: pin names not known; wires that end beside it: INR, INR, A1, CLR, A2
  // Master_Slave_Flip_Flop master_slave_flip_flop_4: pin names not known; wires that end beside it: INR, INR, A2, CLR, A3
endmodule
