// Logisim project Control_Unit.circ as structural Verilog: 1 circuit, main circuit Control_Unit
module Control_Unit (
  input  [15:0] IR,
  input  R,
  input  [3:0] SC,
  input  CLR,
  output [3:0] ALUS,
  output ALUCin,
  output SCCLR,
  output ACLD,
  output ACINR,
  output ACCLR,
  output ARLD,
  output ARINR,
  output ARCLR,
  output DRLD,
  output DRINC,
  output DRCLR,
  output IRLD,
  output IRCLR,
  output READ,
  output WRITE,
  output PCLD,
  output PCINR,
  output PCCLR,
  output TRLD,
  output TRINR,
  output TRCLR,
  output ARE,
  output PCE,
  output DRE,
  output ACE,
  output IRE,
  output TRE,
  output MEME
);

  wire and_1_out, and_2_out, decoder3x8_1_p1, decoder3x8_1_p2, decoder3x8_1_p3, decoder3x8_1_p4,
       decoder3x8_1_p5, decoder3x8_1_p7, decoder3x8_1_p9, decoder3x8_1_p11, not_1_out;
  wire [15:0] decoder4x16_1_p20;

  // Decoder3x8 decoder3x8_1: pin names not known; wires that end beside it: decoder3x8_1_p1, decoder3x8_1_p2, decoder3x8_1_p3, decoder3x8_1_p4, decoder3x8_1_p5, IR[14], decoder3x8_1_p7, IR[13], decoder3x8_1_p9, IR[12], decoder3x8_1_p11
  // Decoder4x16 decoder4x16_1: pin names not known; wires that end beside it: decoder4x16_1_p20[15], SC[0], decoder4x16_1_p20[14], SC[1], decoder4x16_1_p20[13], SC[2], decoder4x16_1_p20[12], SC[3], decoder4x16_1_p20[11], decoder4x16_1_p20[10], decoder4x16_1_p20[9], decoder4x16_1_p20[8], decoder4x16_1_p20[7], decoder4x16_1_p20[6], decoder4x16_1_p20[5], decoder4x16_1_p20[4], decoder4x16_1_p20[3], decoder4x16_1_p20[2], decoder4x16_1_p20[1], decoder4x16_1_p20[0]
  not not_1 (not_1_out, decoder3x8_1_p1);
  and and_1 (and_1_out, not_1_out, IR[15], decoder4x16_1_p20[13]);
  and and_2 (and_2_out, decoder3x8_1_p1, decoder4x16_1_p20[13]);
  ALSU_ControlUnit alsu_controlunit_1 (
    .B7(IR[7]), .B6(IR[6]), .D0(decoder3x8_1_p1), .B9(IR[9]), .D2(decoder3x8_1_p7),
    .T5(decoder4x16_1_p20[10]), .r(and_2_out), .B5(IR[5]), .S(ALUS), .Cin(ALUCin));
  // SC_ControlUnit sc_controlunit_1: pin names not known; wires that end beside it: and_2_out, decoder4x16_1_p20[11], IR[7], decoder3x8_1_p2, decoder4x16_1_p20[8], decoder4x16_1_p20[10], decoder3x8_1_p5, decoder3x8_1_p4, decoder4x16_1_p20[9], decoder3x8_1_p11, decoder3x8_1_p9, decoder3x8_1_p7, decoder3x8_1_p3, CLR, SCCLR
  AC_ControlUnit ac_controlunit_1 (
    .D0(decoder3x8_1_p11), .D1(decoder3x8_1_p9), .D2(decoder3x8_1_p7), .T5(decoder4x16_1_p20[10]),
    .p(and_2_out), .r(and_1_out), .B9(IR[9]), .B7(IR[7]), .B6(IR[6]), .B5(IR[5]), .B11(IR[11]), .CLR(CLR),
    .ACLD(ACLD), .ACINR(ACINR), .ACCLR(ACCLR));
  AR_ControlUnit ar_controlunit_1 (
    .D7(decoder3x8_1_p1), .I(IR[15]), .T3(decoder4x16_1_p20[12]), .T2(decoder4x16_1_p20[13]), .R(R),
    .T0(decoder4x16_1_p20[15]), .D5(decoder3x8_1_p3), .T4(decoder4x16_1_p20[11]), .CLR(CLR), .ARLD(ARLD),
    .ARINR(ARINR), .ARCLR(ARCLR));
  DR_ControlUnit dr_controlunit_1 (
    .D0(decoder3x8_1_p11), .D1(decoder3x8_1_p9), .D2(decoder3x8_1_p7), .D6(decoder3x8_1_p2),
    .T4(decoder4x16_1_p20[11]), .T5(decoder4x16_1_p20[10]), .CLR(CLR), .DRLD(DRLD), .DRINC(DRINC),
    .DRCLR(DRCLR));
  IR_ControlUnit ir_controlunit_1 (.R(R), .T1(decoder4x16_1_p20[14]), .CLR(CLR), .IRLD(IRLD), .IRCLR(IRCLR));
  Mem_ControlUnit mem_controlunit_1 (
    .D7(decoder3x8_1_p1), .I(IR[15]), .T3(decoder4x16_1_p20[12]), .R(R), .T1(decoder4x16_1_p20[14]),
    .D0(decoder3x8_1_p11), .D1(decoder3x8_1_p9), .D2(decoder3x8_1_p7), .D6(decoder3x8_1_p2),
    .T4(decoder4x16_1_p20[11]), .T6(decoder4x16_1_p20[9]), .D5(decoder3x8_1_p3), .D3(decoder3x8_1_p5),
    .READ(READ), .WRITE(WRITE));
  PC_ControlUnit pc_controlunit_1 (
    .D4(decoder3x8_1_p4), .T4(decoder4x16_1_p20[12]), .D5(decoder3x8_1_p3), .T5(decoder4x16_1_p20[11]),
    .R(R), .T1(decoder4x16_1_p20[14]), .T2(and_1_out), .B4(IR[11]), .AC_15(IR[9]), .B3(IR[5]),
    .AC_equals_0(CLR), .s_r(R), .p(decoder4x16_1_p20[15]), .B9(CLR), .PCLD(PCLD), .PCINR(PCINR), .PCCLR(PCCLR));  // open: B2, E_equals_0, B1, FGI, B8, FGO, D6, T6, DR_equals_0, CLR
  TR_ControlUnit tr_controlunit_1 (
    .R(R), .T0(decoder4x16_1_p20[15]), .CLR(CLR), .TRLD(TRLD), .TRINR(TRINR), .TRCLR(TRCLR));
  EnableControlUnit enablecontrolunit_1 (
    .T2(decoder4x16_1_p20[13]), .D4(decoder3x8_1_p4), .T4(decoder4x16_1_p20[11]), .T0(decoder4x16_1_p20[15]),
    .D5(decoder3x8_1_p3), .D0(decoder3x8_1_p11), .T5(decoder4x16_1_p20[10]), .D1(decoder3x8_1_p9),
    .D2(decoder3x8_1_p7), .D6(decoder3x8_1_p2), .T6(decoder4x16_1_p20[9]), .D3(decoder3x8_1_p5),
    .D7(decoder3x8_1_p1), .T3(decoder4x16_1_p20[12]), .B11(IR[11]), .R(R), .T1(decoder4x16_1_p20[14]),
    .I(IR[15]), .EAR(ARE), .EPC(PCE), .EDR(DRE), .EAC(ACE), .EIR(IRE), .ETR(TRE), .EMEM(MEME));

  // Notes on the sheet:
  //   Operation Decoder
  //   D
  //   Sequence Decoder
  //   T
  //   p = D7 I T3
  //   r = D7 I' T3
endmodule
