// Logisim project BasicComputer.circ as structural Verilog: 1 circuit, main circuit CompleteComputer
module CompleteComputer (
);

  wire and_1_out, control_unit_1_acclr, control_unit_1_ace, control_unit_1_acinr, control_unit_1_acld,
       control_unit_1_alucin, control_unit_1_arclr, control_unit_1_are, control_unit_1_arinr,
       control_unit_1_arld, control_unit_1_drclr, control_unit_1_dre, control_unit_1_drinc,
       control_unit_1_drld, control_unit_1_fgiclr, control_unit_1_fgoclr, control_unit_1_ienclr,
       control_unit_1_ienset, control_unit_1_irclr, control_unit_1_ire, control_unit_1_irld,
       control_unit_1_meme, control_unit_1_pcclr, control_unit_1_pce, control_unit_1_pcinr,
       control_unit_1_pcld, control_unit_1_rclr, control_unit_1_read, control_unit_1_rset,
       control_unit_1_scclr, control_unit_1_sclr, control_unit_1_trclr, control_unit_1_tre,
       control_unit_1_trinr, control_unit_1_trld, control_unit_1_write, CP_out, FGI_p5, FGO_p5, IEN_p5,
       keyboard_1_avail, R_p5, Reset_out, S_p5, S_p6;
  wire [3:0] AC_a, AC_a_2, AC_a_3, AC_a_4, control_unit_1_alus, controlled_buffer_1_out,
       controlled_buffer_1_out_2, controlled_buffer_1_out_3, controlled_buffer_3_out, DR_a, DR_a_2, DR_a_3,
       DR_a_4, IR_a, IR_a_2, IR_a_3, IR_a_4, SC_a0;
  wire [6:0] keyboard_1_data;
  wire [7:0] INPR_a, OUTR_a;
  wire [11:0] AR_a, PC_a;
  wire [15:0] bit16_alsu_1_f, ram_1_dout, TR_a;

  Clock CP (.out(CP_out));
  and and_1 (and_1_out, S_p6, CP_out);
  Button Reset (.out(Reset_out));
  Bit4_Counter SC (
    .INR(1'b1), .CP(and_1_out), .CLR(control_unit_1_scclr), .A0(SC_a0[0]), .A1(SC_a0[1]), .A2(SC_a0[2]),
    .A3(SC_a0[3]));
  Hex_Digit_Display hex_digit_display_1 (.value(control_unit_1_alus));  // open: dp
  Control_Unit control_unit_1 (
    .IR({IR_a_4, IR_a_3, IR_a_2, IR_a}), .R(R_p5), .IEN(IEN_p5), .FGI(FGI_p5), .FGO(FGO_p5), .SC(SC_a0),
    .CLR(Reset_out), .ALUS(control_unit_1_alus), .ALUCin(control_unit_1_alucin),
    .SCCLR(control_unit_1_scclr), .ACLD(control_unit_1_acld), .ACINR(control_unit_1_acinr),
    .ACCLR(control_unit_1_acclr), .ARLD(control_unit_1_arld), .ARINR(control_unit_1_arinr),
    .ARCLR(control_unit_1_arclr), .DRLD(control_unit_1_drld), .DRINC(control_unit_1_drinc),
    .DRCLR(control_unit_1_drclr), .IRLD(control_unit_1_irld), .IRCLR(control_unit_1_irclr),
    .READ(control_unit_1_read), .WRITE(control_unit_1_write), .PCLD(control_unit_1_pcld),
    .PCINR(control_unit_1_pcinr), .PCCLR(control_unit_1_pcclr), .TRLD(control_unit_1_trld),
    .TRINR(control_unit_1_trinr), .TRCLR(control_unit_1_trclr), .ARE(control_unit_1_are),
    .PCE(control_unit_1_pce), .DRE(control_unit_1_dre), .ACE(control_unit_1_ace), .IRE(control_unit_1_ire),
    .TRE(control_unit_1_tre), .MEME(control_unit_1_meme), .IENSET(control_unit_1_ienset),
    .IENCLR(control_unit_1_ienclr), .SCLR(control_unit_1_sclr), .RSET(control_unit_1_rset),
    .RCLR(control_unit_1_rclr), .FGICLR(control_unit_1_fgiclr), .FGOCLR(control_unit_1_fgoclr));  // open: ELD, ECLR, ECMP, CPE
  Hex_Digit_Display hex_digit_display_2 (.value(SC_a0));  // open: dp
  Bit16_ALSU bit16_alsu_1 (
    .A({AC_a_4, AC_a_3, AC_a_2, AC_a}), .B({DR_a_4, DR_a_3, DR_a_2, DR_a}), .S(control_unit_1_alus),
    .C_prev(control_unit_1_alucin), .F(bit16_alsu_1_f));  // open: C_next
  Keyboard #(.buflen(8)) keyboard_1 (
    .clk(and_1_out), .avail(keyboard_1_avail), .data(keyboard_1_data));  // open: re, clr
  RAM #(.addrWidth(12), .asyncread("true"), .dataWidth(16)) ram_1 (
    .addr(AR_a), .we(control_unit_1_write), .oe(control_unit_1_read), .clk(and_1_out),
    .din({controlled_buffer_3_out, controlled_buffer_1_out_3, controlled_buffer_1_out_2, controlled_buffer_1_out}),
    .dout(ram_1_dout));
  Bit12_Register AR (
    .I({controlled_buffer_1_out_3, controlled_buffer_1_out_2, controlled_buffer_1_out}),
    .Load(control_unit_1_arld), .INR(control_unit_1_arinr), .CLR(control_unit_1_arclr), .CP(and_1_out),
    .A(AR_a));  // open: C
  Hex_Digit_Display hex_digit_display_3 (.value(AR_a[11:8]));  // open: dp
  Bit12_Register PC (
    .I({controlled_buffer_1_out_3, controlled_buffer_1_out_2, controlled_buffer_1_out}),
    .Load(control_unit_1_pcld), .INR(control_unit_1_pcinr), .CLR(control_unit_1_pcclr), .CP(and_1_out),
    .A(PC_a));  // open: C
  Hex_Digit_Display hex_digit_display_4 (.value(PC_a[11:8]));  // open: dp
  Bit16_Register DR (
    .I({controlled_buffer_3_out, controlled_buffer_1_out_3, controlled_buffer_1_out_2, controlled_buffer_1_out}),
    .Load(control_unit_1_drld), .INR(control_unit_1_drinc), .CLR(control_unit_1_drclr), .CP(and_1_out),
    .A({DR_a_4, DR_a_3, DR_a_2, DR_a}));  // open: C
  Hex_Digit_Display hex_digit_display_5 (.value(DR_a_4));  // open: dp
  Bit16_Register AC (
    .I(bit16_alsu_1_f), .Load(control_unit_1_acld), .INR(control_unit_1_acinr), .CLR(control_unit_1_acclr),
    .CP(and_1_out), .A({AC_a_4, AC_a_3, AC_a_2, AC_a}));  // open: C
  Hex_Digit_Display hex_digit_display_6 (.value(AC_a_4));  // open: dp
  Bit8_Register INPR (
    .I({1'b0, keyboard_1_data}), .Load(keyboard_1_avail), .INR(1'b0), .CLR(Reset_out), .CP(and_1_out),
    .A(INPR_a));  // open: C
  Hex_Digit_Display hex_digit_display_7 (.value(INPR_a[7:4]));  // open: dp
  Bit16_Register IR (
    .I({controlled_buffer_3_out, controlled_buffer_1_out_3, controlled_buffer_1_out_2, controlled_buffer_1_out}),
    .Load(control_unit_1_irld), .INR(1'b0), .CLR(control_unit_1_irclr), .CP(and_1_out),
    .A({IR_a_4, IR_a_3, IR_a_2, IR_a}));  // open: C
  Hex_Digit_Display hex_digit_display_8 (.value(IR_a_4));  // open: dp
  Bit16_Register TR (
    .I({controlled_buffer_3_out, controlled_buffer_1_out_3, controlled_buffer_1_out_2, controlled_buffer_1_out}),
    .Load(control_unit_1_trld), .INR(control_unit_1_trinr), .CLR(control_unit_1_trclr), .CP(and_1_out),
    .A(TR_a));  // open: C
  Hex_Digit_Display hex_digit_display_9 (.value(TR_a[15:12]));  // open: dp
  Bit8_Register OUTR (
    .I({controlled_buffer_3_out, controlled_buffer_1_out_3}), .Load(control_unit_1_fgoclr), .INR(1'b0),
    .CLR(Reset_out), .CP(and_1_out), .A(OUTR_a));  // open: C
  // Master_Slave_Flip_Flop IEN: pin names not known; wires that end beside it: control_unit_1_ienset, and_1_out, control_unit_1_ienclr, Reset_out, IEN_p5
  // Master_Slave_Flip_Flop S: pin names not known; wires that end beside it: control_unit_1_sclr, and_1_out, Reset_out, Reset_out, S_p5, S_p6
  // Master_Slave_Flip_Flop R: pin names not known; wires that end beside it: control_unit_1_rset, and_1_out, control_unit_1_rclr, Reset_out, R_p5
  // Master_Slave_Flip_Flop FGI: pin names not known; wires that end beside it: keyboard_1_avail, and_1_out, control_unit_1_fgiclr, Reset_out, FGI_p5
  // Master_Slave_Flip_Flop FGO: pin names not known; wires that end beside it: 1'b1, and_1_out, control_unit_1_fgoclr, Reset_out, FGO_p5
  Hex_Digit_Display hex_digit_display_10 (.value(ram_1_dout[15:12]));  // open: dp
  Hex_Digit_Display hex_digit_display_11 (.value(ram_1_dout[11:8]));  // open: dp
  Hex_Digit_Display hex_digit_display_12 (.value(AR_a[7:4]));  // open: dp
  Hex_Digit_Display hex_digit_display_13 (.value(AR_a[3:0]));  // open: dp
  Hex_Digit_Display hex_digit_display_14 (.value(PC_a[7:4]));  // open: dp
  Hex_Digit_Display hex_digit_display_15 (.value(PC_a[3:0]));  // open: dp
  Hex_Digit_Display hex_digit_display_16 (.value(DR_a_3));  // open: dp
  Hex_Digit_Display hex_digit_display_17 (.value(DR_a_2));  // open: dp
  Hex_Digit_Display hex_digit_display_18 (.value(AC_a_3));  // open: dp
  Hex_Digit_Display hex_digit_display_19 (.value(AC_a_2));  // open: dp
  Hex_Digit_Display hex_digit_display_20 (.value(INPR_a[3:0]));  // open: dp
  Hex_Digit_Display hex_digit_display_21 (.value(IR_a_3));  // open: dp
  Hex_Digit_Display hex_digit_display_22 (.value(IR_a_2));  // open: dp
  Hex_Digit_Display hex_digit_display_23 (.value(TR_a[11:8]));  // open: dp
  Hex_Digit_Display hex_digit_display_24 (.value(TR_a[7:4]));  // open: dp
  TTY #(.cols(8)) tty_1 (.data(OUTR_a[6:0]), .clk(and_1_out));  // open: we, clr
  LED Done (.in(S_p5));
  Hex_Digit_Display hex_digit_display_25 (.value(ram_1_dout[7:4]));  // open: dp
  Hex_Digit_Display hex_digit_display_26 (.value(ram_1_dout[3:0]));  // open: dp
  Hex_Digit_Display hex_digit_display_27 (.value(DR_a));  // open: dp
  Hex_Digit_Display hex_digit_display_28 (.value(AC_a));  // open: dp
  Hex_Digit_Display hex_digit_display_29 (.value(IR_a));  // open: dp
  Hex_Digit_Display hex_digit_display_30 (.value(TR_a[3:0]));  // open: dp
  assign {controlled_buffer_1_out_3, controlled_buffer_1_out_2, controlled_buffer_1_out} = control_unit_1_are ? AR_a : 12'bz;  // Controlled_Buffer controlled_buffer_1
  assign {controlled_buffer_1_out_3, controlled_buffer_1_out_2, controlled_buffer_1_out} = control_unit_1_pce ? PC_a : 12'bz;  // Controlled_Buffer controlled_buffer_2
  assign {controlled_buffer_3_out, controlled_buffer_1_out_3, controlled_buffer_1_out_2, controlled_buffer_1_out} = control_unit_1_dre ? {DR_a_4, DR_a_3, DR_a_2, DR_a} : 16'bz;  // Controlled_Buffer controlled_buffer_3
  Hex_Digit_Display hex_digit_display_31 (.value(controlled_buffer_3_out));  // open: dp
  Hex_Digit_Display hex_digit_display_32 (.value(controlled_buffer_1_out_3));  // open: dp
  assign {controlled_buffer_3_out, controlled_buffer_1_out_3, controlled_buffer_1_out_2, controlled_buffer_1_out} = control_unit_1_ace ? {AC_a_4, AC_a_3, AC_a_2, AC_a} : 16'bz;  // Controlled_Buffer controlled_buffer_4
  Hex_Digit_Display hex_digit_display_33 (.value(controlled_buffer_1_out_2));  // open: dp
  Hex_Digit_Display hex_digit_display_34 (.value(controlled_buffer_1_out));  // open: dp
  assign {controlled_buffer_3_out, controlled_buffer_1_out_3, controlled_buffer_1_out_2, controlled_buffer_1_out} = control_unit_1_ire ? {IR_a_4, IR_a_3, IR_a_2, IR_a} : 16'bz;  // Controlled_Buffer controlled_buffer_5
  assign {controlled_buffer_3_out, controlled_buffer_1_out_3, controlled_buffer_1_out_2, controlled_buffer_1_out} = control_unit_1_meme ? ram_1_dout : 16'bz;  // Controlled_Buffer controlled_buffer_6
  assign {controlled_buffer_3_out, controlled_buffer_1_out_3, controlled_buffer_1_out_2, controlled_buffer_1_out} = control_unit_1_tre ? TR_a : 16'bz;  // Controlled_Buffer controlled_buffer_7
endmodule
